// Logisim project PROJECT_DATAPATH_ArifurRahaman_2014198642.circ as structural Verilog: 6 circuits, main circuit main
module main (
  output [2:0] RS,
  output [2:0] RT,
  output [31:0] out_3,
  output [31:0] out_4,
  output [31:0] out_5,
  output [31:0] out_6,
  output [2:0] RD,
  output [3:0] opCODE
);

  wire alu_fnc_1_zero, and_1_out, Clk_out, control_unit_1_alu_src, control_unit_1_beq, control_unit_1_binv,
       control_unit_1_cin, control_unit_1_jump, control_unit_1_mem_to_reg, control_unit_1_memory_read,
       control_unit_1_memory_write, control_unit_1_ram_en, control_unit_1_reg_dest, control_unit_1_write_reg,
       RAM_clear_out, REG_clear_out;
  wire [2:0] control_unit_1_aluop, multiplexer_1_out;
  wire [15:0] adder_1_out, adder_2_out, bit_extender_1_out, multiplexer_3_out, multiplexer_4_out,
       register_1_q;
  wire [23:0] bit_extender_3_out;
  wire [31:0] bit_extender_2_out, ram_1_data, register_file_1_read_data_2;

  Button Clk (.out(Clk_out));
  Button REG_clear (.out(REG_clear_out));
  Button RAM_clear (.out(RAM_clear_out));
  Register #(.width(16)) register_1 (.D(multiplexer_4_out), .Q(register_1_q), .clk(Clk_out));  // open: en, clr
  Control_Unit control_unit_1 (
    .clr(opCODE), .Write_Reg(control_unit_1_write_reg), .Binv(control_unit_1_binv), .Cin(control_unit_1_cin),
    .ALUop(control_unit_1_aluop), .MEMORY_Write(control_unit_1_memory_write),
    .MEMORY_Read(control_unit_1_memory_read), .Reg_Dest(control_unit_1_reg_dest), .beq(control_unit_1_beq),
    .jump(control_unit_1_jump), .Mem_to_reg(control_unit_1_mem_to_reg), .ALU_src(control_unit_1_alu_src),
    .Ram_EN(control_unit_1_ram_en));
  ROM #(.addrWidth(16), .dataWidth(13)) rom_1 (.addr(register_1_q), .data({opCODE, RS, RT, RD}));  // open: sel
  assign bit_extender_1_out = {{7{1'b0}}, {RS, RT, RD}};  // Bit_Extender bit_extender_1
  Multiplexer #(.width(3), .enable("false")) multiplexer_1 (
    .in0(RD), .in1(RT), .out(multiplexer_1_out), .sel(control_unit_1_reg_dest));
  Register_File register_file_1 (
    .Write_Register(multiplexer_1_out), .Write_Data(out_6), .RegWrite(control_unit_1_write_reg),
    .Read_Register_1(RS), .Read_Register_2(RT), .Read_Data_2(register_file_1_read_data_2),
    .Read_Data_01(out_3), .clk(Clk_out), .clr(REG_clear_out));
  Multiplexer #(.width(32), .enable("false")) multiplexer_2 (
    .in0(register_file_1_read_data_2), .in1(bit_extender_2_out), .out(out_4), .sel(control_unit_1_alu_src));
  assign bit_extender_2_out = {{29{1'b0}}, RD};  // Bit_Extender bit_extender_2
  Adder #(.width(16)) adder_1 (.a(16'h1), .b(register_1_q), .out(adder_1_out));  // open: cin, cout
  Adder #(.width(16)) adder_2 (.a(adder_1_out), .out(adder_2_out));  // open: b, cin, cout
  ALU__FNC alu_fnc_1 (
    .Cin(control_unit_1_cin), .Binv(control_unit_1_binv), .Zero(alu_fnc_1_zero), .A(out_3), .B(out_4),
    .ALUOP(control_unit_1_aluop), .out_6(out_5));  // open: Cout
  Multiplexer #(.width(16), .enable("false")) multiplexer_3 (
    .in0(adder_1_out), .in1(adder_2_out), .out(multiplexer_3_out), .sel(and_1_out));
  and and_1 (and_1_out, alu_fnc_1_zero, control_unit_1_beq);
  Multiplexer #(.width(16), .enable("false")) multiplexer_4 (
    .in0(multiplexer_3_out), .in1(bit_extender_1_out), .out(multiplexer_4_out), .sel(control_unit_1_jump));
  Bit_Extender #(.in_width(32), .out_width(24)) bit_extender_3 (.in(out_5), .out(bit_extender_3_out));
  Multiplexer #(.width(32), .enable("false")) multiplexer_5 (
    .in0(out_5), .in1(ram_1_data), .out(out_6), .sel(control_unit_1_mem_to_reg));
  RAM #(.addrWidth(24), .dataWidth(32), .bus("separate")) ram_1 (
    .addr(bit_extender_3_out), .din(register_file_1_read_data_2), .data(ram_1_data),
    .str(control_unit_1_memory_write), .sel(control_unit_1_ram_en), .clk(Clk_out),
    .ld(control_unit_1_memory_read), .clr(RAM_clear_out));

  // Notes on the sheet:
  //   contents of rom_1 (hex, n*v repeats v):
  //   0 50e 0 1038 0 23a 0 9c1 1064 7*0 1064
endmodule

module Register_File (
  input  clr,
  input  [2:0] Read_Register_1,
  input  [2:0] Write_Register,
  input  [31:0] Write_Data,
  input  RegWrite,
  input  clk,
  input  [2:0] Read_Register_2,
  output [31:0] Read_Data_01,
  output [31:0] Read_Data_2
);

  wire and_1_out, and_2_out, and_3_out, and_4_out, and_5_out, and_6_out, and_7_out, and_8_out,
       decoder_1_out0, decoder_1_out1, decoder_1_out2, decoder_1_out3, decoder_1_out4, decoder_1_out5,
       decoder_1_out6, decoder_1_out7;
  wire [31:0] R0_q, R1_q, R2_q, R3_q, R4_q, R5_q, R6_q, R7_q;

  Decoder #(.select(3), .enable("false")) decoder_1 (
    .out0(decoder_1_out0), .out1(decoder_1_out1), .out2(decoder_1_out2), .out3(decoder_1_out3),
    .out4(decoder_1_out4), .out5(decoder_1_out5), .out6(decoder_1_out6), .out7(decoder_1_out7),
    .sel(Write_Register));
  and and_1 (and_1_out, decoder_1_out0, RegWrite);
  and and_2 (and_2_out, decoder_1_out1, RegWrite);
  and and_3 (and_3_out, decoder_1_out2, RegWrite);
  and and_4 (and_4_out, decoder_1_out3, RegWrite);
  and and_5 (and_5_out, decoder_1_out4, RegWrite);
  and and_6 (and_6_out, decoder_1_out5, RegWrite);
  and and_7 (and_7_out, decoder_1_out6, RegWrite);
  and and_8 (and_8_out, decoder_1_out7, RegWrite);
  Register #(.width(32)) R0 (.D(Write_Data), .en(and_1_out), .Q(R0_q), .clk(clk), .clr(clr));
  Register #(.width(32)) R1 (.D(Write_Data), .en(and_2_out), .Q(R1_q), .clk(clk), .clr(clr));
  Register #(.width(32)) R2 (.D(Write_Data), .en(and_3_out), .Q(R2_q), .clk(clk), .clr(clr));
  Register #(.width(32)) R3 (.D(Write_Data), .en(and_4_out), .Q(R3_q), .clk(clk), .clr(clr));
  Register #(.width(32)) R4 (.D(Write_Data), .en(and_5_out), .Q(R4_q), .clk(clk), .clr(clr));
  Register #(.width(32)) R5 (.D(Write_Data), .en(and_6_out), .Q(R5_q), .clk(clk), .clr(clr));
  Register #(.width(32)) R6 (.D(Write_Data), .en(and_7_out), .Q(R6_q), .clk(clk), .clr(clr));
  Register #(.width(32)) R7 (.D(Write_Data), .en(and_8_out), .Q(R7_q), .clk(clk), .clr(clr));
  Multiplexer #(.select(3), .width(32), .enable("false")) multiplexer_1 (
    .in0(R0_q), .in1(R1_q), .in2(R2_q), .in3(R3_q), .in4(R4_q), .in5(R5_q), .in6(R6_q), .in7(R7_q),
    .out(Read_Data_01), .sel(Read_Register_1));
  Multiplexer #(.select(3), .width(32), .enable("false")) multiplexer_2 (
    .in0(R0_q), .in1(R1_q), .in2(R2_q), .in3(R3_q), .in4(R4_q), .in5(R5_q), .in6(R6_q), .in7(R7_q),
    .out(Read_Data_2), .sel(Read_Register_2));
endmodule

module _1bit_ALU (
  input  CIN,
  input  A,
  input  B,
  input  [1:0] ALUlop,
  input  Binv,
  output S,
  output COUT
);

  wire adder_1_out, and_1_out, multiplexer_1_out, not_1_out, or_1_out;

  not not_1 (not_1_out, B);
  and and_1 (and_1_out, A, B);
  or or_1 (or_1_out, A, B);
  Multiplexer #(.enable("false")) multiplexer_1 (.in0(B), .in1(not_1_out), .out(multiplexer_1_out), .sel(Binv));
  Adder #(.width(1)) adder_1 (.a(A), .b(multiplexer_1_out), .out(adder_1_out), .cin(CIN), .cout(COUT));
  Multiplexer #(.select(2), .enable("false")) multiplexer_2 (
    .in0(and_1_out), .in1(or_1_out), .in2(adder_1_out), .out(S), .sel(ALUlop));  // open: in3
endmodule

module _16_bit_ALU (
  input  [15:0] A,
  input  [15:0] B,
  input  [1:0] ALUlop,
  input  Cin,
  input  in_5,
  output [15:0] s,
  output ZERO,
  output Over_Flow,
  output out_9
);

  wire n1bit_alu_1_cout, n1bit_alu_2_cout, n1bit_alu_3_cout, n1bit_alu_4_cout, n1bit_alu_5_cout,
       n1bit_alu_6_cout, n1bit_alu_7_cout, n1bit_alu_8_cout, n1bit_alu_9_cout, n1bit_alu_10_cout,
       n1bit_alu_11_cout, n1bit_alu_12_cout, n1bit_alu_13_cout, n1bit_alu_14_cout, n1bit_alu_15_cout;

  _1bit_ALU u_1bit_alu_1 (
    .Binv(in_5), .S(s[0]), .COUT(n1bit_alu_1_cout), .A(A[0]), .B(B[0]), .CIN(Cin), .ALUlop(ALUlop));
  _1bit_ALU u_1bit_alu_2 (
    .Binv(in_5), .S(s[1]), .COUT(n1bit_alu_2_cout), .A(A[1]), .B(B[1]), .CIN(n1bit_alu_1_cout),
    .ALUlop(ALUlop));
  _1bit_ALU u_1bit_alu_3 (
    .Binv(in_5), .S(s[2]), .COUT(n1bit_alu_3_cout), .A(B[2]), .B(A[2]), .CIN(n1bit_alu_2_cout),
    .ALUlop(ALUlop));
  _1bit_ALU u_1bit_alu_4 (
    .Binv(in_5), .S(s[3]), .COUT(n1bit_alu_4_cout), .A(A[3]), .B(B[3]), .CIN(n1bit_alu_3_cout),
    .ALUlop(ALUlop));
  _1bit_ALU u_1bit_alu_5 (
    .Binv(in_5), .S(s[4]), .COUT(n1bit_alu_5_cout), .A(A[4]), .B(B[4]), .CIN(n1bit_alu_4_cout),
    .ALUlop(ALUlop));
  _1bit_ALU u_1bit_alu_6 (
    .Binv(in_5), .S(s[5]), .COUT(n1bit_alu_6_cout), .A(A[5]), .B(B[5]), .CIN(n1bit_alu_5_cout),
    .ALUlop(ALUlop));
  _1bit_ALU u_1bit_alu_7 (
    .Binv(in_5), .S(s[6]), .COUT(n1bit_alu_7_cout), .A(A[6]), .B(B[6]), .CIN(n1bit_alu_6_cout),
    .ALUlop(ALUlop));
  _1bit_ALU u_1bit_alu_8 (
    .Binv(in_5), .S(s[7]), .COUT(n1bit_alu_8_cout), .A(A[7]), .B(B[7]), .CIN(n1bit_alu_7_cout),
    .ALUlop(ALUlop));
  _1bit_ALU u_1bit_alu_9 (
    .Binv(in_5), .S(s[8]), .COUT(n1bit_alu_9_cout), .A(A[8]), .B(B[8]), .CIN(n1bit_alu_8_cout),
    .ALUlop(ALUlop));
  _1bit_ALU u_1bit_alu_10 (
    .Binv(in_5), .S(s[9]), .COUT(n1bit_alu_10_cout), .A(A[9]), .B(B[9]), .CIN(n1bit_alu_9_cout),
    .ALUlop(ALUlop));
  _1bit_ALU u_1bit_alu_11 (
    .Binv(in_5), .S(s[10]), .COUT(n1bit_alu_11_cout), .A(A[10]), .B(B[10]), .CIN(n1bit_alu_10_cout),
    .ALUlop(ALUlop));
  _1bit_ALU u_1bit_alu_12 (
    .Binv(in_5), .S(s[11]), .COUT(n1bit_alu_12_cout), .A(A[11]), .B(B[11]), .CIN(n1bit_alu_11_cout),
    .ALUlop(ALUlop));
  _1bit_ALU u_1bit_alu_13 (
    .Binv(in_5), .S(s[12]), .COUT(n1bit_alu_13_cout), .A(A[12]), .B(B[12]), .CIN(n1bit_alu_12_cout),
    .ALUlop(ALUlop));
  _1bit_ALU u_1bit_alu_14 (
    .Binv(in_5), .S(s[13]), .COUT(n1bit_alu_14_cout), .A(A[13]), .B(B[13]), .CIN(n1bit_alu_13_cout),
    .ALUlop(ALUlop));
  _1bit_ALU u_1bit_alu_15 (
    .Binv(in_5), .S(s[14]), .COUT(n1bit_alu_15_cout), .A(A[14]), .B(B[14]), .CIN(n1bit_alu_14_cout),
    .ALUlop(ALUlop));
  _1bit_ALU u_1bit_alu_16 (
    .Binv(in_5), .S(s[15]), .COUT(out_9), .A(A[15]), .B(B[15]), .CIN(n1bit_alu_15_cout), .ALUlop(ALUlop));
  xor xor_1 (Over_Flow, n1bit_alu_15_cout, out_9);
  ExactlyOne xor_2 (
    .out(ZERO), .in0(s[0]), .in1(s[1]), .in2(s[2]), .in3(s[3]), .in4(s[4]), .in5(s[5]), .in6(s[6]),
    .in7(s[7]), .in8(s[8]), .in9(s[9]), .in10(s[10]), .in11(s[11]), .in12(s[12]), .in13(s[13]), .in14(s[14]),
    .in15(s[15]));
endmodule

module ALU__FNC (
  input  [31:0] A,
  input  [31:0] B,
  input  [2:0] ALUOP,
  input  Cin,
  input  Binv,
  output [31:0] out_6,
  output Zero,
  output Cout
);

  wire comparator_1_gt, comparator_1_lt;
  wire [4:0] bit_extender_1_out, bit_extender_2_out;
  wire [31:0] adder_1_out, and_1_out, bit_extender_3_out, multiplexer_1_out, not_1_out, shifter_1_out,
       shifter_2_out, undriven;

  assign not_1_out = ~B;  // NOT_Gate not_1, 32 bits wide
  Bit_Extender #(.in_width(32), .out_width(5)) bit_extender_1 (.in(B), .out(bit_extender_1_out));
  Bit_Extender #(.in_width(32), .out_width(5)) bit_extender_2 (.in(B), .out(bit_extender_2_out));
  assign and_1_out = A & B;  // AND_Gate and_1, 32 bits wide
  Multiplexer #(.width(32), .enable("false")) multiplexer_1 (
    .in0(B), .in1(not_1_out), .out(multiplexer_1_out), .sel(Binv));
  Comparator #(.width(32)) comparator_1 (.a(A), .b(B), .gt(comparator_1_gt), .eq(Zero), .lt(comparator_1_lt));
  Adder #(.width(32)) adder_1 (.a(A), .b(multiplexer_1_out), .out(adder_1_out), .cin(Cin), .cout(Cout));
  Shifter #(.width(32)) shifter_1 (.in(A), .\dist (bit_extender_1_out), .out(shifter_1_out));
  Shifter #(.width(32), .shift("lr")) shifter_2 (.in(A), .\dist (bit_extender_2_out), .out(shifter_2_out));
  assign bit_extender_3_out = {{31{1'b0}}, comparator_1_lt};  // Bit_Extender bit_extender_3
  Multiplexer #(.select(3), .width(32), .enable("false")) multiplexer_2 (
    .in0(undriven), .in1(adder_1_out), .in2(bit_extender_3_out), .in3(shifter_1_out), .in4(shifter_2_out),
    .in5(and_1_out), .out(out_6), .sel(ALUOP));  // open: in6, in7

  // Notes on the sheet:
  //   3
  //   4
  //   5
  //   1
  //   2
endmodule

module Control_Unit (
  input  [3:0] clr,
  output Write_Reg,
  output Binv,
  output Cin,
  output [2:0] ALUop,
  output MEMORY_Write,
  output MEMORY_Read,
  output Reg_Dest,
  output beq,
  output jump,
  output Mem_to_reg,
  output ALU_src,
  output Ram_EN
);

  wire decoder_1_out0, decoder_1_out3, decoder_1_out5, decoder_1_out7, decoder_1_out9, decoder_1_out10;

  Decoder #(.select(4)) decoder_1 (
    .out0(decoder_1_out0), .out1(MEMORY_Write), .out2(Binv), .out3(decoder_1_out3), .out4(beq),
    .out5(decoder_1_out5), .out6(jump), .out7(decoder_1_out7), .out8(Mem_to_reg), .out9(decoder_1_out9),
    .out10(decoder_1_out10), .sel(clr));  // open: out11, out12, out13, out14, out15, en
  or or_1 (Write_Reg, Binv, decoder_1_out3, decoder_1_out5, decoder_1_out7, Mem_to_reg, decoder_1_out9, decoder_1_out10);
  or or_2 (ALUop[0], MEMORY_Write, Binv, beq, decoder_1_out5, decoder_1_out7, Mem_to_reg, decoder_1_out9, decoder_1_out10);
  or or_3 (ALUop[1], decoder_1_out3, beq, decoder_1_out5, jump);
  or or_4 (ALUop[2], beq, jump, decoder_1_out10);
  or or_5 (Reg_Dest, MEMORY_Write, beq, decoder_1_out5, Mem_to_reg, decoder_1_out9);
  or or_6 (ALU_src, MEMORY_Write, decoder_1_out5, Mem_to_reg, decoder_1_out9);
  or or_7 (Ram_EN, MEMORY_Write, Mem_to_reg);

  assign Cin = Binv;
  assign MEMORY_Read = Mem_to_reg;
endmodule
